# Fritzing sketch CH32V003-Blink-Deluxe (saved by Fritzing 1.0.6)
perfboards: 1
breadboards: 1

parts:
  S2 = Momentary Switch 6mm 2pin
  S3 = Momentary Switch 6mm 2pin
  S4 = Momentary Switch 6mm 2pin
  SG1 = Buzzer 12mm [part_number=COM-07950 package=buzzer-12mm-ns]
  R1 = Resistor [tolerance=±5% power=0.25W resistance=220 package=THT]
  LED1 = LED - 5mm [color="Red (633nm)" current=0.030A package="5 mm [THT]"]
  LED2 = LED - 5mm [color="Yellow (595nm)" current=0.030A package="5 mm [THT]"]
  LED3 = LED - 5mm [color="Green (570nm)" current=0.030A package="5 mm [THT]"]
  R2 = Resistor [tolerance=±5% power=0.25W resistance=220 package=THT]
  R3 = Resistor [tolerance=±5% power=0.25W resistance=220 package=THT]
  R4 = Resistor [tolerance=±5% power=0.25W resistance=220 package=THT]

nets:
  N1: S2.1, S3.1, S4.1
  N2: SG1.1, R4.Pin_1
  N3: R1.Pin_0, R2.Pin_0, R3.Pin_0, R4.Pin_0
  N4: R1.Pin_1, LED1.cathode
  N5: LED2.cathode, R2.Pin_1
  N6: LED3.cathode, R3.Pin_1

notes:
  CH32V003 開発ボード
  ブレッドボード 400H
  USB 端子が右側になるように取り付ける
  タクトスイッチ
  パッシブブザー
  ⊕印が右側になるように取り付ける
  LED
  200Ω
  100Ω
  アノード（足の長い方）が右側になるように取り付ける

custom parts:
  Momentary Switch 6mm 2pin: Momentary Switch 6mm 2 pin Button commonly used for reset or general input.
  Buzzer 12mm: Buzzer 12mm Spark Fun Electronics SKU : Comp-Buzzer Through hole This is a small 12mm round speaker that operates around the audible 2kHz range. You can use these speakers to create simple music or user interfaces. This is not a true piezoelectric speaker but behaves similarly. Instead of a piezoelectric crystal that vibrates with an electric current, this tiny speaker uses an electromagnet to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
